# Fritzing sketch Untitled Sketch (saved by Fritzing 0.8.7b)
breadboards: 1

parts:
  Mod1 = KY-015 Temperature & Humidity Sensor Module [package="Breakout board"]
  e-radionica_com1 = LM393 LDR breakout [part_number=100027]
  U1 = NodeMCU V3.0

nets:
  VIN: Mod1.Vin, e-radionica_com1.GND, e-radionica_com1.AO, U1.D4, U1.Vin
  N1: Mod1.-, U1.GND

custom parts:
  KY-015 Temperature & Humidity Sensor Module: KY-015 temperature and humidity sensor module, provides a low-latency serial interface to measure humidity and temperature.
  NodeMCU V3.0: ESP8266 based NodeMCU
